# Fritzing sketch drink_alert (saved by Fritzing 0.9.3b)
breadboards: 1

parts:
  Heltec_New_WiFi_Kit_1 = Heltec New WiFi Kit 32 [part_number=ZC-47]
  Part1 = GY-VL53L0XV2 Laser Ranger Module
  Part2 = Passive Buzzer
  GY1 = MPU-6050 Board GY-521 [form="♀ (female)" package=THT]
  Mod1 = KY-003 Hall Magnetic Sensor Module [package="Breakout board"]

nets:
  N1: Heltec_New_WiFi_Kit_1.pin_23, Part2.S
  N2: Heltec_New_WiFi_Kit_1.pin_24, Mod1.S
  N3: Heltec_New_WiFi_Kit_1.pin_32, Part1.SDA, GY1.pin4
  N4: Heltec_New_WiFi_Kit_1.pin_33, Part1.SCL, GY1.pin3
  VCC: Heltec_New_WiFi_Kit_1.pin_16, Heltec_New_WiFi_Kit_1.pin_20, Part1.VCC, GY1.pin1, Mod1.Vin
  GND: Heltec_New_WiFi_Kit_1.pin_18, Heltec_New_WiFi_Kit_1.pin_19, Part1.GND, Part2.GND, GY1.pin2, Mod1.-
  N5: Heltec_New_WiFi_Kit_1.pin_17, Part2.NC
  N6: Heltec_New_WiFi_Kit_1.pin_21, Heltec_New_WiFi_Kit_1.pin_15

custom parts:
  GY-VL53L0XV2 Laser Ranger Module: The GY-VL53L0XV2 is based on the VL53L0X from ST Microelectronics, a time-of-flight ranging system integrated into a compact module.
  MPU-6050 Board GY-521: Acelerometro y Giroscopio MPU-6050 Board GY-521
  KY-003 Hall Magnetic Sensor Module: KEYES KY-003 Arduino Hall Magnetic Sensor Module is a switch that will turn on/off in the presence of a magnetic field.
