# Fritzing sketch touch_beep (saved by Fritzing 0.9.3b)
breadboards: 1

parts:
  Heltec_New_WiFi_Kit_1 = Heltec New WiFi Kit 32 [part_number=ZC-47]
  Part2 = Passive Buzzer

nets:
  N1: Heltec_New_WiFi_Kit_1.pin_23, Part2.S
  N2: Heltec_New_WiFi_Kit_1.pin_16, Heltec_New_WiFi_Kit_1.pin_20
  N3: Heltec_New_WiFi_Kit_1.pin_18, Heltec_New_WiFi_Kit_1.pin_19, Part2.GND
  N4: Heltec_New_WiFi_Kit_1.pin_17, Part2.NC
  N5: Heltec_New_WiFi_Kit_1.pin_21, Heltec_New_WiFi_Kit_1.pin_15
