# Fritzing sketch tripwire (saved by Fritzing 0.9.3b)
breadboards: 1

parts:
  Heltec_New_WiFi_Kit_1 = Heltec New WiFi Kit 32 [part_number=ZC-47]
  Part1 = GY-VL53L0XV2 Laser Ranger Module
  Part2 = Passive Buzzer

nets:
  N1: Heltec_New_WiFi_Kit_1.pin_23, Part2.S
  N2: Heltec_New_WiFi_Kit_1.pin_32, Part1.SDA
  N3: Heltec_New_WiFi_Kit_1.pin_33, Part1.SCL
  N4: Heltec_New_WiFi_Kit_1.pin_16, Heltec_New_WiFi_Kit_1.pin_20, Part1.VCC
  GND: Heltec_New_WiFi_Kit_1.pin_18, Heltec_New_WiFi_Kit_1.pin_19, Part1.GND, Part2.GND
  N5: Heltec_New_WiFi_Kit_1.pin_17, Part2.NC
  N6: Heltec_New_WiFi_Kit_1.pin_21, Heltec_New_WiFi_Kit_1.pin_15

custom parts:
  GY-VL53L0XV2 Laser Ranger Module: The GY-VL53L0XV2 is based on the VL53L0X from ST Microelectronics, a time-of-flight ranging system integrated into a compact module.
